# Fritzing sketch keys (saved by Fritzing 0.9.1b)
breadboards: 1

parts:
  MUX = 74HC4052 [package=dil16]
  Часть1 = Arduino Uno (Rev3)
  DIN1 = DIN-5 jack (MIDI) [package=THT]
  R1 = Resistor [tolerance=±5% resistance=220k package=THT]
  R3 = Resistor [tolerance=±5% resistance=220 package=THT]
  IN = male pin header, 8 pins [form="♂ (male)"]
  OUT = male pin header, 8 pins [form="♂ (male)"]
  SHIFT = 74HC595 [package="DIP16 [THT]"]
  R4 = Resistor [tolerance=±5% resistance=10k package=THT]
  R5 = Resistor [tolerance=±5% resistance=10k package=THT]

nets:
  N1: MUX.Y0, IN.pin5
  N2: MUX.Y2, IN.pin7
  N3: MUX.Y, Часть1.D2, R5.Pin_1
  N4: MUX.Y3, IN.pin8
  N5: MUX.Y1, IN.pin6
  GND: MUX.INH, MUX.VEE, MUX.GND, Часть1.GND, DIN1.2, DIN1.GND, SHIFT.GND, SHIFT.OE, R4.Pin_0, R5.Pin_0
  N6: MUX.B, Часть1.D7
  N7: MUX.A, Часть1.D6_PWM
  N8: MUX.X3, IN.pin4
  N9: MUX.X0, IN.pin1
  N10: MUX.X, Часть1.D3_PWM, R4.Pin_1
  N11: MUX.X1, IN.pin2
  N12: MUX.X2, IN.pin3
  VCC: MUX.VCC, Часть1.5V, R1.Pin_0, SHIFT.MR, SHIFT.VCC
  N13: Часть1.D10_PWM/SS, SHIFT.DS
  N14: Часть1.D11_PWM/MOSI, SHIFT.ST_CP
  N15: Часть1.D12/MISO, SHIFT.SH_CP
  N16: Часть1.D1/TX, R3.Pin_0
  N17: DIN1.5, R3.Pin_1
  N18: DIN1.4, R1.Pin_1
  N19: OUT.pin1, SHIFT.Q0
  N20: OUT.pin2, SHIFT.Q1
  N21: OUT.pin3, SHIFT.Q2
  N22: OUT.pin4, SHIFT.Q3
  N23: OUT.pin5, SHIFT.Q4
  N24: OUT.pin6, SHIFT.Q5
  N25: OUT.pin7, SHIFT.Q6
  N26: OUT.pin8, SHIFT.Q7
