# Fritzing sketch keys_ps (saved by Fritzing 0.9.1b)
stripboards: 1

parts:
  U2 = 74HC4052 [package=dil16]
  Часть1 = Arduino Uno (Rev3)
  DIN1 = DIN-5 jack (MIDI) [package=THT]
  R1 = Resistor [tolerance=±5% resistance=220 package=THT]
  R3 = Resistor [tolerance=±5% resistance=220 package=THT]
  J1 = male pin header, 8 pins [form="♂ (male)"]
  J2 = male pin header, 8 pins [form="♂ (male)"]
  U5 = 74HC595 [package="DIP16 [THT]"]
  Pad1 = Pad [width=7.90222222222222 height=9.03111111111111 connect=center]  # not connected
  R5 = Resistor [tolerance=±5% resistance=10k package=THT]
  R4 = Resistor [tolerance=±5% resistance=10k package=THT]

nets:
  N1: U2.Y0, J1.pin5
  N2: U2.Y2, J1.pin7
  N3: U2.Y, Часть1.D2, R5.Pin_1
  N4: U2.Y3, J1.pin8
  N5: U2.Y1, J1.pin6
  GND: U2.INH, U2.VEE, U2.GND, Часть1.GND, DIN1.2, DIN1.GND, U5.GND, U5.OE, R5.Pin_0, R4.Pin_0
  N6: U2.B, Часть1.D7
  N7: U2.A, Часть1.D6_PWM
  N8: U2.X3, J1.pin4
  N9: U2.X0, J1.pin1
  N10: U2.X, Часть1.D3_PWM, R4.Pin_1
  N11: U2.X1, J1.pin2
  N12: U2.X2, J1.pin3
  VCC: U2.VCC, Часть1.5V, R1.Pin_0, U5.MR, U5.VCC
  N13: Часть1.D10_PWM/SS, U5.DS
  N14: Часть1.D11_PWM/MOSI, U5.ST_CP
  N15: Часть1.D12/MISO, U5.SH_CP
  N16: Часть1.D1/TX, R3.Pin_0
  N17: DIN1.5, R3.Pin_1
  N18: DIN1.4, R1.Pin_1
  N19: J2.pin1, U5.Q0
  N20: J2.pin2, U5.Q1
  N21: J2.pin3, U5.Q2
  N22: J2.pin4, U5.Q3
  N23: J2.pin5, U5.Q4
  N24: J2.pin6, U5.Q5
  N25: J2.pin7, U5.Q6
  N26: J2.pin8, U5.Q7

notes:
  Orange wires are in fact direct connections to Arduino ports
  Long black (GND) and white (+5V) wires on this side are not needed on a real proto board
  Most wires are connected on the bottom side of the proto board
  Black wires - GND
  White wires - +5
  Other colors - random purpose
